# Fritzing sketch emitter1b (saved by Fritzing 0.9.9b)
circuit board: 2.5cm x 2.5cm
perfboards: 1

parts:
  RLED = Resistor [tolerance=±5% resistance=100 package=THT]
  HLIR = LED - 5mm [color="Infrared (940nm)" part_number=TSAL6100 package="5 mm [THT]"]
  HLLED = LED - 3mm [color="Orange (612nm)" package="3 mm [THT]"]
  VTIR = NPN-Transistor [package="TO92 [THT]"]
  RIR = Resistor [tolerance=±5% resistance=22 package=THT]
  J5V = male pin header, 1 pin [form="♂ (male)"]
  JGND = male pin header, 1 pin [form="♂ (male)"]
  JIR = male pin header, 1 pin [form="♂ (male)"]
  JLED = male pin header, 1 pin [form="♂ (male)"]

nets:
  N1: RLED.Pin_0, JLED.pin1
  N2: RLED.Pin_1, HLLED.anode
  N3: HLIR.cathode, VTIR.C
  N4: HLIR.anode, RIR.Pin_1
  N5: HLLED.cathode, VTIR.E, JGND.pin1
  N6: VTIR.B, JIR.pin1
  N7: RIR.Pin_0, J5V.pin1
